// Logisim project app.circ as structural Verilog: 1 circuit, main circuit main
module main (
);

  wire and_4_out, and_5_out, CLK, CLK_5, comparator_1_eq, comparator_2_eq, comparator_3_gt, comparator_4_eq,
       comparator_4_lt, comparator_5_gt, comparator_6_eq, comparator_6_lt, not_1_out, not_2_out, P1_ADD_SHIP,
       P1_CHECK_SHIP, P1_CONF, P1_CURR_SEG_ALIVE, P1_NEXT_SHIP, P1_RO_ROTATED, P1_ROTATED,
       P1_SHIP_DRAW_ENABLE, P1_WIN, P2_ADD_SHIP, P2_CHECK_SHIP, P2_CONF, P2_CURR_SEG_ALIVE, P2_NEXT_SHIP,
       P2_RO_ROTATED, P2_ROTATED, P2_SHIP_DRAW_ENABLE, P2_WIN, PREP_PHASE_END, undriven, undriven_2;
  wire [1:0] P1_RO_SHIP_TYPE, P1_SEG_SEL, P2_RO_SHIP_TYPE, P2_SEG_SEL;
  wire [2:0] P1_SHIP_DRAW_SEL, P2_SHIP_DRAW_SEL;
  wire [3:0] P1_CUR_X, P1_CUR_Y, P1_CURR_SHIP_ADD, P1_RO_ALIVE, P1_RO_SHIP_X, P1_RO_SHIP_Y, P2_CUR_X,
       P2_CUR_Y, P2_CURR_SHIP_ADD, P2_RO_ALIVE, P2_RO_SHIP_X, P2_RO_SHIP_Y;
  wire [4:0] P1_CUR_BL_SEL, P1_CUR_BR_SEL, P1_CUR_TL_SEL, P1_CUR_TR_SEL, P1_SHIP_BL_SEL, P1_SHIP_BR_SEL,
       P1_SHIP_TL_SEL, P1_SHIP_TR_SEL, P2_CUR_BL_SEL, P2_CUR_BR_SEL, P2_CUR_TL_SEL, P2_CUR_TR_SEL,
       P2_SHIP_BL_SEL, P2_SHIP_BR_SEL, P2_SHIP_TL_SEL, P2_SHIP_TR_SEL;
  wire [5:0] main_7_out_x_00, main_7_out_x_01, main_7_out_x_10, main_7_out_x_11, main_7_out_y_00,
       main_7_out_y_01, main_7_out_y_10, main_7_out_y_11, main_15_out_x_00, main_15_out_x_01,
       main_15_out_x_10, main_15_out_x_11, main_15_out_y_00, main_15_out_y_01, main_15_out_y_10,
       main_15_out_y_11, P1_SHIP_SCR_X, P1_SHIP_SCR_Y, P2_SHIP_SCR_X, P2_SHIP_SCR_Y;
  wire [6:0] keyboard_1_data, keyboard_2_data;
  wire [29:0] main_2_bl_data, main_2_br_data, main_2_tl_data, main_2_tr_data, main_3_out_0, main_3_out_1,
       main_3_out_1a, main_3_out_1b, main_3_out_1c, main_3_out_1d, main_3_out_2, main_3_out_3, main_3_out_4,
       main_3_out_5, main_3_out_6, main_3_out_7, main_3_out_8, main_3_out_9, main_3_out_10, main_3_out_11,
       main_3_out_12, main_3_out_13, main_3_out_14, main_3_out_15, main_3_out_16, main_3_out_17,
       main_3_out_18, main_3_out_19, main_3_out_a, main_3_out_b, main_3_out_c, main_3_out_d, main_3_out_e,
       main_3_out_f, main_4_out_0, main_4_out_1, main_4_out_1a, main_4_out_1b, main_4_out_1c, main_4_out_1d,
       main_4_out_2, main_4_out_3, main_4_out_4, main_4_out_5, main_4_out_6, main_4_out_7, main_4_out_8,
       main_4_out_9, main_4_out_10, main_4_out_11, main_4_out_12, main_4_out_13, main_4_out_14,
       main_4_out_15, main_4_out_16, main_4_out_17, main_4_out_18, main_4_out_19, main_4_out_a, main_4_out_b,
       main_4_out_c, main_4_out_d, main_4_out_e, main_4_out_f, main_5_out_0, main_5_out_1, main_5_out_1a,
       main_5_out_1b, main_5_out_1c, main_5_out_1d, main_5_out_2, main_5_out_3, main_5_out_4, main_5_out_5,
       main_5_out_6, main_5_out_7, main_5_out_8, main_5_out_9, main_5_out_10, main_5_out_11, main_5_out_12,
       main_5_out_13, main_5_out_14, main_5_out_15, main_5_out_16, main_5_out_17, main_5_out_18,
       main_5_out_19, main_5_out_a, main_5_out_b, main_5_out_c, main_5_out_d, main_5_out_e, main_5_out_f,
       main_6_out_0, main_6_out_1, main_6_out_1a, main_6_out_1b, main_6_out_1c, main_6_out_1d, main_6_out_2,
       main_6_out_3, main_6_out_4, main_6_out_5, main_6_out_6, main_6_out_7, main_6_out_8, main_6_out_9,
       main_6_out_10, main_6_out_11, main_6_out_12, main_6_out_13, main_6_out_14, main_6_out_15,
       main_6_out_16, main_6_out_17, main_6_out_18, main_6_out_19, main_6_out_a, main_6_out_b, main_6_out_c,
       main_6_out_d, main_6_out_e, main_6_out_f, main_10_bl_data, main_10_br_data, main_10_tl_data,
       main_10_tr_data, main_11_out_0, main_11_out_1, main_11_out_1a, main_11_out_1b, main_11_out_1c,
       main_11_out_1d, main_11_out_2, main_11_out_3, main_11_out_4, main_11_out_5, main_11_out_6,
       main_11_out_7, main_11_out_8, main_11_out_9, main_11_out_10, main_11_out_11, main_11_out_12,
       main_11_out_13, main_11_out_14, main_11_out_15, main_11_out_16, main_11_out_17, main_11_out_18,
       main_11_out_19, main_11_out_a, main_11_out_b, main_11_out_c, main_11_out_d, main_11_out_e,
       main_11_out_f, main_12_out_0, main_12_out_1, main_12_out_1a, main_12_out_1b, main_12_out_1c,
       main_12_out_1d, main_12_out_2, main_12_out_3, main_12_out_4, main_12_out_5, main_12_out_6,
       main_12_out_7, main_12_out_8, main_12_out_9, main_12_out_10, main_12_out_11, main_12_out_12,
       main_12_out_13, main_12_out_14, main_12_out_15, main_12_out_16, main_12_out_17, main_12_out_18,
       main_12_out_19, main_12_out_a, main_12_out_b, main_12_out_c, main_12_out_d, main_12_out_e,
       main_12_out_f, main_13_out_0, main_13_out_1, main_13_out_1a, main_13_out_1b, main_13_out_1c,
       main_13_out_1d, main_13_out_2, main_13_out_3, main_13_out_4, main_13_out_5, main_13_out_6,
       main_13_out_7, main_13_out_8, main_13_out_9, main_13_out_10, main_13_out_11, main_13_out_12,
       main_13_out_13, main_13_out_14, main_13_out_15, main_13_out_16, main_13_out_17, main_13_out_18,
       main_13_out_19, main_13_out_a, main_13_out_b, main_13_out_c, main_13_out_d, main_13_out_e,
       main_13_out_f, main_14_out_0, main_14_out_1, main_14_out_1a, main_14_out_1b, main_14_out_1c,
       main_14_out_1d, main_14_out_2, main_14_out_3, main_14_out_4, main_14_out_5, main_14_out_6,
       main_14_out_7, main_14_out_8, main_14_out_9, main_14_out_10, main_14_out_11, main_14_out_12,
       main_14_out_13, main_14_out_14, main_14_out_15, main_14_out_16, main_14_out_17, main_14_out_18,
       main_14_out_19, main_14_out_a, main_14_out_b, main_14_out_c, main_14_out_d, main_14_out_e,
       main_14_out_f, P1_CUR_BL_DATA, P1_CUR_BR_DATA, P1_CUR_TL_DATA, P1_CUR_TR_DATA, P1_SHIP_BL_DATA,
       P1_SHIP_BR_DATA, P1_SHIP_TL_DATA, P1_SHIP_TR_DATA, P2_CUR_BL_DATA, P2_CUR_BR_DATA, P2_CUR_TL_DATA,
       P2_CUR_TR_DATA, P2_SHIP_BL_DATA, P2_SHIP_BR_DATA, P2_SHIP_TL_DATA, P2_SHIP_TR_DATA;

  Clock clock_1 (.out(CLK));
  Counter #(.width(3), .max('h4)) counter_1 (.carry(CLK_5), .clk(CLK));  // open: load, D, count, Q, clr
  Counter #(.width(2), .max('h3)) counter_2 (
    .Q(P1_SEG_SEL), .carry(P1_NEXT_SHIP), .clk(CLK_5));  // open: load, D, count, clr
  memory_management_main main_1 (
    .X(P1_CUR_X), .Y(P1_CUR_Y), .ROTATED(P1_ROTATED),
    .RAM_OUT({P1_RO_ALIVE, P1_RO_ROTATED, P1_RO_SHIP_TYPE, P1_RO_SHIP_Y, P1_RO_SHIP_X}), .CHECK_X(P2_CUR_X),
    .CHECK_Y(P2_CUR_Y), .SINK_IF_HIT(1'b1), .CONFIRM(P1_ADD_SHIP), .CHECK(P2_CHECK_SHIP), .CLK(CLK),
    .SHOW_NEXT_SHIP(P1_NEXT_SHIP), .WIN(P1_WIN), .CURR_SHIP_ADD(P1_CURR_SHIP_ADD));  // open: HIT, CHECKING
  Keyboard keyboard_1 (.clk(CLK), .clr(undriven), .data(keyboard_1_data));  // open: re, avail
  cursor_module_main main_2 (
    .CUR_X(P1_CUR_X), .CLK(CLK), .KEYBOARD_OUT(keyboard_1_data), .KEYBOARD_RST(undriven),
    .TL_SEL(P1_CUR_TL_SEL), .TR_SEL(P1_CUR_TR_SEL), .BL_SEL(P1_CUR_BL_SEL), .BR_SEL(P1_CUR_BR_SEL),
    .TL_DATA(main_2_tl_data), .TR_DATA(main_2_tr_data), .BL_DATA(main_2_bl_data), .BR_DATA(main_2_br_data),
    .CONFIRM(P1_CONF), .CUR_Y(P1_CUR_Y), .ROTATED(P1_ROTATED));
  demuxor_30x30x3_main main_3 (
    .DATA_1(P1_SHIP_TL_DATA), .SELECT_1(P1_SHIP_TL_SEL), .SELECT_0(P1_CUR_TL_SEL), .DATA_0(P1_CUR_TL_DATA),
    .OUT_0(main_3_out_0), .OUT_1(main_3_out_1), .OUT_2(main_3_out_2), .OUT_3(main_3_out_3),
    .OUT_4(main_3_out_4), .OUT_6(main_3_out_6), .OUT_7(main_3_out_7), .OUT_8(main_3_out_8),
    .OUT_9(main_3_out_9), .OUT_a(main_3_out_a), .OUT_c(main_3_out_c), .OUT_12(main_3_out_12),
    .OUT_d(main_3_out_d), .OUT_13(main_3_out_13), .OUT_e(main_3_out_e), .OUT_14(main_3_out_14),
    .OUT_f(main_3_out_f), .OUT_15(main_3_out_15), .OUT_10(main_3_out_10), .OUT_16(main_3_out_16),
    .OUT_18(main_3_out_18), .OUT_19(main_3_out_19), .OUT_1a(main_3_out_1a), .OUT_1b(main_3_out_1b),
    .OUT_1c(main_3_out_1c), .OUT_5(main_3_out_5), .OUT_b(main_3_out_b), .OUT_11(main_3_out_11),
    .OUT_17(main_3_out_17), .OUT_1d(main_3_out_1d));  // open: SELECT_2, DATA_2
  DotMatrix #(.matrixcols(30), .matrixrows(30), .persist(500)) dotmatrix_1 (
    .col0(main_3_out_0), .col1(main_3_out_1), .col2(main_3_out_2), .col3(main_3_out_3), .col4(main_3_out_4),
    .col5(main_3_out_5), .col6(main_3_out_6), .col7(main_3_out_7), .col8(main_3_out_8), .col9(main_3_out_9),
    .col10(main_3_out_a), .col11(main_3_out_b), .col12(main_3_out_c), .col13(main_3_out_d),
    .col14(main_3_out_e), .col15(main_3_out_f), .col16(main_3_out_10), .col17(main_3_out_11),
    .col18(main_3_out_12), .col19(main_3_out_13), .col20(main_3_out_14), .col21(main_3_out_15),
    .col22(main_3_out_16), .col23(main_3_out_17), .col24(main_3_out_18), .col25(main_3_out_19),
    .col26(main_3_out_1a), .col27(main_3_out_1b), .col28(main_3_out_1c), .col29(main_3_out_1d));
  DotMatrix #(.matrixcols(30), .matrixrows(30), .persist(500)) dotmatrix_2 (
    .col0(main_4_out_0), .col1(main_4_out_1), .col2(main_4_out_2), .col3(main_4_out_3), .col4(main_4_out_4),
    .col5(main_4_out_5), .col6(main_4_out_6), .col7(main_4_out_7), .col8(main_4_out_8), .col9(main_4_out_9),
    .col10(main_4_out_a), .col11(main_4_out_b), .col12(main_4_out_c), .col13(main_4_out_d),
    .col14(main_4_out_e), .col15(main_4_out_f), .col16(main_4_out_10), .col17(main_4_out_11),
    .col18(main_4_out_12), .col19(main_4_out_13), .col20(main_4_out_14), .col21(main_4_out_15),
    .col22(main_4_out_16), .col23(main_4_out_17), .col24(main_4_out_18), .col25(main_4_out_19),
    .col26(main_4_out_1a), .col27(main_4_out_1b), .col28(main_4_out_1c), .col29(main_4_out_1d));
  demuxor_30x30x3_main main_4 (
    .DATA_1(P1_SHIP_BL_DATA), .SELECT_1(P1_SHIP_BL_SEL), .SELECT_0(P1_CUR_BL_SEL), .DATA_0(P1_CUR_BL_DATA),
    .OUT_0(main_4_out_0), .OUT_1(main_4_out_1), .OUT_2(main_4_out_2), .OUT_3(main_4_out_3),
    .OUT_4(main_4_out_4), .OUT_6(main_4_out_6), .OUT_7(main_4_out_7), .OUT_8(main_4_out_8),
    .OUT_9(main_4_out_9), .OUT_a(main_4_out_a), .OUT_c(main_4_out_c), .OUT_12(main_4_out_12),
    .OUT_d(main_4_out_d), .OUT_13(main_4_out_13), .OUT_e(main_4_out_e), .OUT_14(main_4_out_14),
    .OUT_f(main_4_out_f), .OUT_15(main_4_out_15), .OUT_10(main_4_out_10), .OUT_16(main_4_out_16),
    .OUT_18(main_4_out_18), .OUT_19(main_4_out_19), .OUT_1a(main_4_out_1a), .OUT_1b(main_4_out_1b),
    .OUT_1c(main_4_out_1c), .OUT_5(main_4_out_5), .OUT_b(main_4_out_b), .OUT_11(main_4_out_11),
    .OUT_17(main_4_out_17), .OUT_1d(main_4_out_1d));  // open: SELECT_2, DATA_2
  assign P1_CUR_TL_DATA = not_1_out ? main_2_tl_data : 30'bz;  // Controlled_Buffer controlled_buffer_1
  assign P1_CUR_TR_DATA = not_1_out ? main_2_tr_data : 30'bz;  // Controlled_Buffer controlled_buffer_2
  assign P1_CUR_BL_DATA = not_1_out ? main_2_bl_data : 30'bz;  // Controlled_Buffer controlled_buffer_3
  assign P1_CUR_BR_DATA = not_1_out ? main_2_br_data : 30'bz;  // Controlled_Buffer controlled_buffer_4
  not not_1 (not_1_out, PREP_PHASE_END);
  Comparator #(.width(4), .mode("unsigned")) comparator_1 (
    .a(P1_CURR_SHIP_ADD), .b(4'b1010), .eq(comparator_1_eq));  // open: gt, lt
  Comparator #(.width(4), .mode("unsigned")) comparator_2 (
    .a(4'b1010), .b(P2_CURR_SHIP_ADD), .eq(comparator_2_eq));  // open: gt, lt
  Multiplexer #(.select(2), .enable("false")) multiplexer_1 (
    .in0(P1_RO_ALIVE[0]), .in1(P1_RO_ALIVE[1]), .in2(P1_RO_ALIVE[2]), .in3(P1_RO_ALIVE[3]),
    .out(P1_CURR_SEG_ALIVE), .sel(P1_SEG_SEL));
  and and_1 (PREP_PHASE_END, comparator_1_eq, comparator_2_eq);
  Multiplexer #(.width(3), .enable("false")) multiplexer_2 (
    .in0(3'b010), .in1(3'b001), .out(P1_SHIP_DRAW_SEL), .sel(P1_CURR_SEG_ALIVE));
  demuxor_30x30x3_main main_5 (
    .DATA_1(P1_SHIP_TR_DATA), .SELECT_1(P1_SHIP_TR_SEL), .SELECT_0(P1_CUR_TR_SEL), .DATA_0(P1_CUR_TR_DATA),
    .OUT_0(main_5_out_0), .OUT_1(main_5_out_1), .OUT_2(main_5_out_2), .OUT_3(main_5_out_3),
    .OUT_4(main_5_out_4), .OUT_6(main_5_out_6), .OUT_7(main_5_out_7), .OUT_8(main_5_out_8),
    .OUT_9(main_5_out_9), .OUT_a(main_5_out_a), .OUT_c(main_5_out_c), .OUT_12(main_5_out_12),
    .OUT_d(main_5_out_d), .OUT_13(main_5_out_13), .OUT_e(main_5_out_e), .OUT_14(main_5_out_14),
    .OUT_f(main_5_out_f), .OUT_15(main_5_out_15), .OUT_10(main_5_out_10), .OUT_16(main_5_out_16),
    .OUT_18(main_5_out_18), .OUT_19(main_5_out_19), .OUT_1a(main_5_out_1a), .OUT_1b(main_5_out_1b),
    .OUT_1c(main_5_out_1c), .OUT_5(main_5_out_5), .OUT_b(main_5_out_b), .OUT_11(main_5_out_11),
    .OUT_17(main_5_out_17), .OUT_1d(main_5_out_1d));  // open: SELECT_2, DATA_2
  DotMatrix #(.matrixcols(30), .matrixrows(30), .persist(500)) dotmatrix_3 (
    .col0(main_5_out_0), .col1(main_5_out_1), .col2(main_5_out_2), .col3(main_5_out_3), .col4(main_5_out_4),
    .col5(main_5_out_5), .col6(main_5_out_6), .col7(main_5_out_7), .col8(main_5_out_8), .col9(main_5_out_9),
    .col10(main_5_out_a), .col11(main_5_out_b), .col12(main_5_out_c), .col13(main_5_out_d),
    .col14(main_5_out_e), .col15(main_5_out_f), .col16(main_5_out_10), .col17(main_5_out_11),
    .col18(main_5_out_12), .col19(main_5_out_13), .col20(main_5_out_14), .col21(main_5_out_15),
    .col22(main_5_out_16), .col23(main_5_out_17), .col24(main_5_out_18), .col25(main_5_out_19),
    .col26(main_5_out_1a), .col27(main_5_out_1b), .col28(main_5_out_1c), .col29(main_5_out_1d));
  demuxor_30x30x3_main main_6 (
    .DATA_1(P1_SHIP_BR_DATA), .SELECT_1(P1_SHIP_BR_SEL), .SELECT_0(P1_CUR_BR_SEL), .DATA_0(P1_CUR_BR_DATA),
    .OUT_0(main_6_out_0), .OUT_1(main_6_out_1), .OUT_2(main_6_out_2), .OUT_3(main_6_out_3),
    .OUT_4(main_6_out_4), .OUT_6(main_6_out_6), .OUT_7(main_6_out_7), .OUT_8(main_6_out_8),
    .OUT_9(main_6_out_9), .OUT_a(main_6_out_a), .OUT_c(main_6_out_c), .OUT_12(main_6_out_12),
    .OUT_d(main_6_out_d), .OUT_13(main_6_out_13), .OUT_e(main_6_out_e), .OUT_14(main_6_out_14),
    .OUT_f(main_6_out_f), .OUT_15(main_6_out_15), .OUT_10(main_6_out_10), .OUT_16(main_6_out_16),
    .OUT_18(main_6_out_18), .OUT_19(main_6_out_19), .OUT_1a(main_6_out_1a), .OUT_1b(main_6_out_1b),
    .OUT_1c(main_6_out_1c), .OUT_5(main_6_out_5), .OUT_b(main_6_out_b), .OUT_11(main_6_out_11),
    .OUT_17(main_6_out_17), .OUT_1d(main_6_out_1d));  // open: SELECT_2, DATA_2
  DotMatrix #(.matrixcols(30), .matrixrows(30), .persist(500)) dotmatrix_4 (
    .col0(main_6_out_0), .col1(main_6_out_1), .col2(main_6_out_2), .col3(main_6_out_3), .col4(main_6_out_4),
    .col5(main_6_out_5), .col6(main_6_out_6), .col7(main_6_out_7), .col8(main_6_out_8), .col9(main_6_out_9),
    .col10(main_6_out_a), .col11(main_6_out_b), .col12(main_6_out_c), .col13(main_6_out_d),
    .col14(main_6_out_e), .col15(main_6_out_f), .col16(main_6_out_10), .col17(main_6_out_11),
    .col18(main_6_out_12), .col19(main_6_out_13), .col20(main_6_out_14), .col21(main_6_out_15),
    .col22(main_6_out_16), .col23(main_6_out_17), .col24(main_6_out_18), .col25(main_6_out_19),
    .col26(main_6_out_1a), .col27(main_6_out_1b), .col28(main_6_out_1c), .col29(main_6_out_1d));
  and and_2 (P1_ADD_SHIP, P1_CONF, ~PREP_PHASE_END);  // AND_Gate
  and and_3 (P1_CHECK_SHIP, P1_CONF, PREP_PHASE_END);
  Comparator #(.width(4), .mode("unsigned")) comparator_3 (
    .a(P1_CURR_SHIP_ADD), .b(4'b0000), .gt(comparator_3_gt));  // open: eq, lt
  ship_xyr_to_screen_xy_main main_7 (
    .in_1(P1_RO_SHIP_X), .in_2(P1_RO_SHIP_Y), .in_3(P1_RO_ROTATED), .OUT_X_00(main_7_out_x_00),
    .OUT_Y_00(main_7_out_y_00), .OUT_X_01(main_7_out_x_01), .OUT_Y_01(main_7_out_y_01),
    .OUT_X_10(main_7_out_x_10), .OUT_Y_10(main_7_out_y_10), .OUT_X_11(main_7_out_x_11),
    .OUT_Y_11(main_7_out_y_11));
  screen_xy_to_screen_data_main main_8 (
    .SCREEN_X(P1_SHIP_SCR_X), .SCREEN_Y(P1_SHIP_SCR_Y), .DATA_TO_DISPLAY(P1_SHIP_DRAW_SEL),
    .TL_SEL_OUT(P1_SHIP_TL_SEL), .TR_SEL_OUT(P1_SHIP_TR_SEL), .BL_SEL_OUT(P1_SHIP_BL_SEL),
    .BR_SEL_OUT(P1_SHIP_BR_SEL), .TL_DATA_OUT(P1_SHIP_TL_DATA), .TR_DATA_OUT(P1_SHIP_TR_DATA),
    .BL_DATA_OUT(P1_SHIP_BL_DATA), .BR_DATA_OUT(P1_SHIP_BR_DATA), .CLK(CLK), .ENABLE(and_4_out));
  and and_4 (and_4_out, P1_SHIP_DRAW_ENABLE, comparator_3_gt);
  Comparator #(.width(2), .mode("unsigned")) comparator_4 (
    .a(P1_SEG_SEL), .b(P1_RO_SHIP_TYPE), .eq(comparator_4_eq), .lt(comparator_4_lt));  // open: gt
  or or_1 (P1_SHIP_DRAW_ENABLE, comparator_4_eq, comparator_4_lt);
  Multiplexer #(.select(2), .width(6), .enable("false")) multiplexer_3 (
    .in0(main_7_out_x_00), .in1(main_7_out_x_01), .in2(main_7_out_x_10), .in3(main_7_out_x_11),
    .out(P1_SHIP_SCR_X), .sel(P1_SEG_SEL));
  Multiplexer #(.select(2), .width(6), .enable("false")) multiplexer_4 (
    .in0(main_7_out_y_00), .in1(main_7_out_y_01), .in2(main_7_out_y_10), .in3(main_7_out_y_11),
    .out(P1_SHIP_SCR_Y), .sel(P1_SEG_SEL));
  Counter #(.width(2), .max('h3)) counter_3 (
    .Q(P2_SEG_SEL), .carry(P2_NEXT_SHIP), .clk(CLK_5));  // open: load, D, count, clr
  memory_management_main main_9 (
    .X(P2_CUR_X), .Y(P2_CUR_Y), .ROTATED(P2_ROTATED),
    .RAM_OUT({P2_RO_ALIVE, P2_RO_ROTATED, P2_RO_SHIP_TYPE, P2_RO_SHIP_Y, P2_RO_SHIP_X}), .CHECK_X(P1_CUR_X),
    .CHECK_Y(P1_CUR_Y), .SINK_IF_HIT(1'b1), .CONFIRM(P2_ADD_SHIP), .CHECK(P1_CHECK_SHIP), .CLK(CLK),
    .SHOW_NEXT_SHIP(P2_NEXT_SHIP), .WIN(P2_WIN), .CURR_SHIP_ADD(P2_CURR_SHIP_ADD));  // open: HIT, CHECKING
  Keyboard keyboard_2 (.clk(CLK), .clr(undriven_2), .data(keyboard_2_data));  // open: re, avail
  cursor_module_main main_10 (
    .CUR_X(P2_CUR_X), .CLK(CLK), .KEYBOARD_OUT(keyboard_2_data), .KEYBOARD_RST(undriven_2),
    .TL_SEL(P2_CUR_TL_SEL), .TR_SEL(P2_CUR_TR_SEL), .BL_SEL(P2_CUR_BL_SEL), .BR_SEL(P2_CUR_BR_SEL),
    .TL_DATA(main_10_tl_data), .TR_DATA(main_10_tr_data), .BL_DATA(main_10_bl_data),
    .BR_DATA(main_10_br_data), .CONFIRM(P2_CONF), .CUR_Y(P2_CUR_Y), .ROTATED(P2_ROTATED));
  demuxor_30x30x3_main main_11 (
    .DATA_1(P2_SHIP_TL_DATA), .SELECT_1(P2_SHIP_TL_SEL), .SELECT_0(P2_CUR_TL_SEL), .DATA_0(P2_CUR_TL_DATA),
    .OUT_0(main_11_out_0), .OUT_1(main_11_out_1), .OUT_2(main_11_out_2), .OUT_3(main_11_out_3),
    .OUT_4(main_11_out_4), .OUT_6(main_11_out_6), .OUT_7(main_11_out_7), .OUT_8(main_11_out_8),
    .OUT_9(main_11_out_9), .OUT_a(main_11_out_a), .OUT_c(main_11_out_c), .OUT_12(main_11_out_12),
    .OUT_d(main_11_out_d), .OUT_13(main_11_out_13), .OUT_e(main_11_out_e), .OUT_14(main_11_out_14),
    .OUT_f(main_11_out_f), .OUT_15(main_11_out_15), .OUT_10(main_11_out_10), .OUT_16(main_11_out_16),
    .OUT_18(main_11_out_18), .OUT_19(main_11_out_19), .OUT_1a(main_11_out_1a), .OUT_1b(main_11_out_1b),
    .OUT_1c(main_11_out_1c), .OUT_5(main_11_out_5), .OUT_b(main_11_out_b), .OUT_11(main_11_out_11),
    .OUT_17(main_11_out_17), .OUT_1d(main_11_out_1d));  // open: SELECT_2, DATA_2
  DotMatrix #(.matrixcols(30), .matrixrows(30), .persist(500)) dotmatrix_5 (
    .col0(main_11_out_0), .col1(main_11_out_1), .col2(main_11_out_2), .col3(main_11_out_3),
    .col4(main_11_out_4), .col5(main_11_out_5), .col6(main_11_out_6), .col7(main_11_out_7),
    .col8(main_11_out_8), .col9(main_11_out_9), .col10(main_11_out_a), .col11(main_11_out_b),
    .col12(main_11_out_c), .col13(main_11_out_d), .col14(main_11_out_e), .col15(main_11_out_f),
    .col16(main_11_out_10), .col17(main_11_out_11), .col18(main_11_out_12), .col19(main_11_out_13),
    .col20(main_11_out_14), .col21(main_11_out_15), .col22(main_11_out_16), .col23(main_11_out_17),
    .col24(main_11_out_18), .col25(main_11_out_19), .col26(main_11_out_1a), .col27(main_11_out_1b),
    .col28(main_11_out_1c), .col29(main_11_out_1d));
  DotMatrix #(.matrixcols(30), .matrixrows(30), .persist(500)) dotmatrix_6 (
    .col0(main_12_out_0), .col1(main_12_out_1), .col2(main_12_out_2), .col3(main_12_out_3),
    .col4(main_12_out_4), .col5(main_12_out_5), .col6(main_12_out_6), .col7(main_12_out_7),
    .col8(main_12_out_8), .col9(main_12_out_9), .col10(main_12_out_a), .col11(main_12_out_b),
    .col12(main_12_out_c), .col13(main_12_out_d), .col14(main_12_out_e), .col15(main_12_out_f),
    .col16(main_12_out_10), .col17(main_12_out_11), .col18(main_12_out_12), .col19(main_12_out_13),
    .col20(main_12_out_14), .col21(main_12_out_15), .col22(main_12_out_16), .col23(main_12_out_17),
    .col24(main_12_out_18), .col25(main_12_out_19), .col26(main_12_out_1a), .col27(main_12_out_1b),
    .col28(main_12_out_1c), .col29(main_12_out_1d));
  demuxor_30x30x3_main main_12 (
    .DATA_1(P2_SHIP_BL_DATA), .SELECT_1(P2_SHIP_BL_SEL), .SELECT_0(P2_CUR_BL_SEL), .DATA_0(P2_CUR_BL_DATA),
    .OUT_0(main_12_out_0), .OUT_1(main_12_out_1), .OUT_2(main_12_out_2), .OUT_3(main_12_out_3),
    .OUT_4(main_12_out_4), .OUT_6(main_12_out_6), .OUT_7(main_12_out_7), .OUT_8(main_12_out_8),
    .OUT_9(main_12_out_9), .OUT_a(main_12_out_a), .OUT_c(main_12_out_c), .OUT_12(main_12_out_12),
    .OUT_d(main_12_out_d), .OUT_13(main_12_out_13), .OUT_e(main_12_out_e), .OUT_14(main_12_out_14),
    .OUT_f(main_12_out_f), .OUT_15(main_12_out_15), .OUT_10(main_12_out_10), .OUT_16(main_12_out_16),
    .OUT_18(main_12_out_18), .OUT_19(main_12_out_19), .OUT_1a(main_12_out_1a), .OUT_1b(main_12_out_1b),
    .OUT_1c(main_12_out_1c), .OUT_5(main_12_out_5), .OUT_b(main_12_out_b), .OUT_11(main_12_out_11),
    .OUT_17(main_12_out_17), .OUT_1d(main_12_out_1d));  // open: SELECT_2, DATA_2
  assign P2_CUR_TL_DATA = not_2_out ? main_10_tl_data : 30'bz;  // Controlled_Buffer controlled_buffer_5
  assign P2_CUR_TR_DATA = not_2_out ? main_10_tr_data : 30'bz;  // Controlled_Buffer controlled_buffer_6
  assign P2_CUR_BL_DATA = not_2_out ? main_10_bl_data : 30'bz;  // Controlled_Buffer controlled_buffer_7
  assign P2_CUR_BR_DATA = not_2_out ? main_10_br_data : 30'bz;  // Controlled_Buffer controlled_buffer_8
  not not_2 (not_2_out, PREP_PHASE_END);
  Multiplexer #(.select(2), .enable("false")) multiplexer_5 (
    .in0(P2_RO_ALIVE[0]), .in1(P2_RO_ALIVE[1]), .in2(P2_RO_ALIVE[2]), .in3(P2_RO_ALIVE[3]),
    .out(P2_CURR_SEG_ALIVE), .sel(P2_SEG_SEL));
  Multiplexer #(.width(3), .enable("false")) multiplexer_6 (
    .in0(3'b010), .in1(3'b001), .out(P2_SHIP_DRAW_SEL), .sel(P2_CURR_SEG_ALIVE));
  demuxor_30x30x3_main main_13 (
    .DATA_1(P2_SHIP_BR_DATA), .SELECT_1(P2_SHIP_BR_SEL), .SELECT_0(P2_CUR_BR_SEL), .DATA_0(P2_CUR_BR_DATA),
    .OUT_0(main_13_out_0), .OUT_1(main_13_out_1), .OUT_2(main_13_out_2), .OUT_3(main_13_out_3),
    .OUT_4(main_13_out_4), .OUT_6(main_13_out_6), .OUT_7(main_13_out_7), .OUT_8(main_13_out_8),
    .OUT_9(main_13_out_9), .OUT_a(main_13_out_a), .OUT_c(main_13_out_c), .OUT_12(main_13_out_12),
    .OUT_d(main_13_out_d), .OUT_13(main_13_out_13), .OUT_e(main_13_out_e), .OUT_14(main_13_out_14),
    .OUT_f(main_13_out_f), .OUT_15(main_13_out_15), .OUT_10(main_13_out_10), .OUT_16(main_13_out_16),
    .OUT_18(main_13_out_18), .OUT_19(main_13_out_19), .OUT_1a(main_13_out_1a), .OUT_1b(main_13_out_1b),
    .OUT_1c(main_13_out_1c), .OUT_5(main_13_out_5), .OUT_b(main_13_out_b), .OUT_11(main_13_out_11),
    .OUT_17(main_13_out_17), .OUT_1d(main_13_out_1d));  // open: SELECT_2, DATA_2
  DotMatrix #(.matrixcols(30), .matrixrows(30), .persist(500)) dotmatrix_7 (
    .col0(main_14_out_0), .col1(main_14_out_1), .col2(main_14_out_2), .col3(main_14_out_3),
    .col4(main_14_out_4), .col5(main_14_out_5), .col6(main_14_out_6), .col7(main_14_out_7),
    .col8(main_14_out_8), .col9(main_14_out_9), .col10(main_14_out_a), .col11(main_14_out_b),
    .col12(main_14_out_c), .col13(main_14_out_d), .col14(main_14_out_e), .col15(main_14_out_f),
    .col16(main_14_out_10), .col17(main_14_out_11), .col18(main_14_out_12), .col19(main_14_out_13),
    .col20(main_14_out_14), .col21(main_14_out_15), .col22(main_14_out_16), .col23(main_14_out_17),
    .col24(main_14_out_18), .col25(main_14_out_19), .col26(main_14_out_1a), .col27(main_14_out_1b),
    .col28(main_14_out_1c), .col29(main_14_out_1d));
  demuxor_30x30x3_main main_14 (
    .DATA_1(P2_SHIP_TR_DATA), .SELECT_1(P2_SHIP_TR_SEL), .SELECT_0(P2_CUR_TR_SEL), .DATA_0(P2_CUR_TR_DATA),
    .OUT_0(main_14_out_0), .OUT_1(main_14_out_1), .OUT_2(main_14_out_2), .OUT_3(main_14_out_3),
    .OUT_4(main_14_out_4), .OUT_6(main_14_out_6), .OUT_7(main_14_out_7), .OUT_8(main_14_out_8),
    .OUT_9(main_14_out_9), .OUT_a(main_14_out_a), .OUT_c(main_14_out_c), .OUT_12(main_14_out_12),
    .OUT_d(main_14_out_d), .OUT_13(main_14_out_13), .OUT_e(main_14_out_e), .OUT_14(main_14_out_14),
    .OUT_f(main_14_out_f), .OUT_15(main_14_out_15), .OUT_10(main_14_out_10), .OUT_16(main_14_out_16),
    .OUT_18(main_14_out_18), .OUT_19(main_14_out_19), .OUT_1a(main_14_out_1a), .OUT_1b(main_14_out_1b),
    .OUT_1c(main_14_out_1c), .OUT_5(main_14_out_5), .OUT_b(main_14_out_b), .OUT_11(main_14_out_11),
    .OUT_17(main_14_out_17), .OUT_1d(main_14_out_1d));  // open: SELECT_2, DATA_2
  DotMatrix #(.matrixcols(30), .matrixrows(30), .persist(500)) dotmatrix_8 (
    .col0(main_13_out_0), .col1(main_13_out_1), .col2(main_13_out_2), .col3(main_13_out_3),
    .col4(main_13_out_4), .col5(main_13_out_5), .col6(main_13_out_6), .col7(main_13_out_7),
    .col8(main_13_out_8), .col9(main_13_out_9), .col10(main_13_out_a), .col11(main_13_out_b),
    .col12(main_13_out_c), .col13(main_13_out_d), .col14(main_13_out_e), .col15(main_13_out_f),
    .col16(main_13_out_10), .col17(main_13_out_11), .col18(main_13_out_12), .col19(main_13_out_13),
    .col20(main_13_out_14), .col21(main_13_out_15), .col22(main_13_out_16), .col23(main_13_out_17),
    .col24(main_13_out_18), .col25(main_13_out_19), .col26(main_13_out_1a), .col27(main_13_out_1b),
    .col28(main_13_out_1c), .col29(main_13_out_1d));
  Comparator #(.width(4), .mode("unsigned")) comparator_5 (
    .a(P2_CURR_SHIP_ADD), .b(4'b0000), .gt(comparator_5_gt));  // open: eq, lt
  ship_xyr_to_screen_xy_main main_15 (
    .in_1(P2_RO_SHIP_X), .in_2(P2_RO_SHIP_Y), .in_3(P2_RO_ROTATED), .OUT_X_00(main_15_out_x_00),
    .OUT_Y_00(main_15_out_y_00), .OUT_X_01(main_15_out_x_01), .OUT_Y_01(main_15_out_y_01),
    .OUT_X_10(main_15_out_x_10), .OUT_Y_10(main_15_out_y_10), .OUT_X_11(main_15_out_x_11),
    .OUT_Y_11(main_15_out_y_11));
  screen_xy_to_screen_data_main main_16 (
    .SCREEN_X(P2_SHIP_SCR_X), .SCREEN_Y(P2_SHIP_SCR_Y), .DATA_TO_DISPLAY(P2_SHIP_DRAW_SEL),
    .TL_SEL_OUT(P2_SHIP_TL_SEL), .TR_SEL_OUT(P2_SHIP_TR_SEL), .BL_SEL_OUT(P2_SHIP_BL_SEL),
    .BR_SEL_OUT(P2_SHIP_BR_SEL), .TL_DATA_OUT(P2_SHIP_TL_DATA), .TR_DATA_OUT(P2_SHIP_TR_DATA),
    .BL_DATA_OUT(P2_SHIP_BL_DATA), .BR_DATA_OUT(P2_SHIP_BR_DATA), .CLK(CLK), .ENABLE(and_5_out));
  and and_5 (and_5_out, P2_SHIP_DRAW_ENABLE, comparator_5_gt);
  and and_6 (P2_ADD_SHIP, P2_CONF, ~PREP_PHASE_END);  // AND_Gate
  and and_7 (P2_CHECK_SHIP, P2_CONF, PREP_PHASE_END);
  Comparator #(.width(2), .mode("unsigned")) comparator_6 (
    .a(P2_SEG_SEL), .b(P2_RO_SHIP_TYPE), .eq(comparator_6_eq), .lt(comparator_6_lt));  // open: gt
  or or_2 (P2_SHIP_DRAW_ENABLE, comparator_6_eq, comparator_6_lt);
  Multiplexer #(.select(2), .width(6), .enable("false")) multiplexer_7 (
    .in0(main_15_out_x_00), .in1(main_15_out_x_01), .in2(main_15_out_x_10), .in3(main_15_out_x_11),
    .out(P2_SHIP_SCR_X), .sel(P2_SEG_SEL));
  Multiplexer #(.select(2), .width(6), .enable("false")) multiplexer_8 (
    .in0(main_15_out_y_00), .in1(main_15_out_y_01), .in2(main_15_out_y_10), .in3(main_15_out_y_11),
    .out(P2_SHIP_SCR_Y), .sel(P2_SEG_SEL));

  // Notes on the sheet:
  //   sunk
  //   alive
  //   1 jak gracze wybiora statki juz
  //   STATKI GRACZA 1
  //   sunk
  //   alive
  //   STATKI GRACZA 2
endmodule
