// Logisim project arrow.circ as structural Verilog: 1 circuit, main circuit main
module main (
  input  \input ,
  output [4:0] output4,
  output [4:0] output5,
  output [4:0] output3,
  output [4:0] output6,
  output [4:0] output2,
  output [4:0] output7,
  output [4:0] output1,
  output [4:0] output8
);

  Multiplexer #(.width(30), .enable("false")) multiplexer_1 (
    .in0(30'h8427dc4), .in1(30'h8ef9084), .out({output2, output3, output4, output5, output6, output7}),
    .sel(\input ));

  assign output1 = {5{1'b0}};
  assign output8 = {5{1'b0}};
endmodule
