// Logisim project memory_management.circ as structural Verilog: 1 circuit, main circuit main
// 2
module main (
  input  [3:0] X,
  input  CLK,
  input  [3:0] Y,
  input  ROTATED,
  input  CONFIRM,
  input  SHOW_NEXT_SHIP,
  input  [3:0] CHECK_X,
  input  [3:0] CHECK_Y,
  input  CHECK,
  input  SINK_IF_HIT,
  output WIN,
  output HIT,
  output [14:0] RAM_OUT,
  output CHECKING
);

  wire _0HIT, _1HIT, _2HIT, _3HIT, ALIVE0, ALIVE1, ALIVE2, ALIVE3, and_1_out, and_2_out, and_8_out,
       and_9_out, and_10_out, and_11_out, and_12_out, and_13_out, and_14_out, and_15_out, and_16_out,
       and_17_out, and_18_out, CHECK_FRAME_END, CHECK_OCCUPIED_RST, comparator_1_eq, comparator_2_eq,
       comparator_3_eq, comparator_4_eq, comparator_5_eq, comparator_6_eq, comparator_7_eq, comparator_8_eq,
       comparator_9_eq, comparator_10_eq, comparator_11_eq, comparator_12_eq, HORI_HIT, main_1_p3, main_3_p4,
       main_4_p6, main_4_p7, MEM_NOT_CHANGING, not_1_out, not_2_out, not_3_out, not_4_out, not_5_out,
       not_6_out, or_1_out, or_2_out, or_3_out, or_4_out, OVERWRITE, ROTATED_CHECK, SAVE,
       SAVE_CURR_RAM_STATE, VERT_HIT;
  wire [1:0] SHIP_TYPE;
  wire [2:0] counter_3_q;
  wire [3:0] adder_1_out, adder_2_out, adder_3_out, adder_4_out, adder_5_out, adder_6_out, and_3_out,
       CURR_SHIP_CHECK, CURRENT_SHIP, MEM_SELECT, multiplexer_1_out;
  wire [4:0] hits_counter_q;
  wire [7:0] HORI_CHECK, VERT_CHECK;
  wire [9:0] register_1_q;
  wire [14:0] RAM_OUT_t, SHIP_DATA;

  Multiplexer #(.select(2), .width(4), .enable("false")) multiplexer_1 (
    .in0(4'b0001), .in1(4'b0011), .in2(4'b0111), .in3(4'b1111), .out(multiplexer_1_out), .sel(SHIP_TYPE));
  assign RAM_OUT_t = SAVE ? SHIP_DATA : 15'bz;  // Controlled_Buffer controlled_buffer_1
  not not_1 (not_1_out, SAVE);
  Register #(.width(15)) register_1 (
    .D(RAM_OUT_t), .Q({ALIVE3, ALIVE2, ALIVE1, ALIVE0, ROTATED_CHECK, register_1_q}),
    .clk(SAVE_CURR_RAM_STATE));  // open: en, clr
  and and_1 (and_1_out, HORI_HIT, ~ROTATED_CHECK);  // AND_Gate
  and and_2 (and_2_out, ROTATED_CHECK, VERT_HIT);
  not not_2 (not_2_out, CHECKING);
  RAM #(.addrWidth(4), .dataWidth(15)) ram_1 (
    .addr(MEM_SELECT), .data(RAM_OUT_t), .clk(CLK), .ld(not_1_out));  // open: sel, clr
  D_Flip_Flop d_ff_1 (.clk(CHECK), .D(CHECK), .Q(CHECKING), .reset(CHECK_OCCUPIED_RST));  // open: Qn, preset, en
  Demultiplexer #(.width(8), .enable("false")) demultiplexer_1 (
    .out0(HORI_CHECK), .out1(VERT_CHECK), .in(register_1_q[7:0]), .sel(ROTATED_CHECK));
  or or_1 (or_1_out, and_1_out, and_2_out);
  Counter #(.width(4), .max('h9), .trigger("falling")) counter_1 (
    .Q(CURRENT_SHIP), .clk(or_2_out));  // open: load, D, count, carry, clr
  or or_2 (or_2_out, SHOW_NEXT_SHIP, CONFIRM);
  assign RAM_OUT = not_2_out ? RAM_OUT_t : 15'bz;  // Controlled_Buffer controlled_buffer_2
  and and_3 (and_3_out[0], ALIVE0, ~_0HIT);  // AND_Gate
  and and_4 (and_3_out[1], ALIVE1, ~_1HIT);  // AND_Gate
  and and_5 (and_3_out[2], ALIVE2, ~_2HIT);  // AND_Gate
  and and_6 (and_3_out[3], ALIVE3, ~_3HIT);  // AND_Gate
  and and_7 (OVERWRITE, SINK_IF_HIT, or_1_out);
  assign SHIP_DATA = not_3_out ? {multiplexer_1_out, ROTATED, SHIP_TYPE, Y, X} : 15'bz;  // Controlled_Buffer controlled_buffer_3
  not not_3 (not_3_out, CHECKING);
  assign SHIP_DATA = CHECKING ? {and_3_out, ROTATED_CHECK, register_1_q} : 15'bz;  // Controlled_Buffer controlled_buffer_4
  assign MEM_SELECT = not_4_out ? CURRENT_SHIP : 4'bz;  // Controlled_Buffer controlled_buffer_5
  not not_4 (not_4_out, CHECKING);
  assign MEM_SELECT = CHECKING ? CURR_SHIP_CHECK : 4'bz;  // Controlled_Buffer controlled_buffer_6
  // _4bit_greater_or_equal_than_and_less_than__main main_1: pin names not known; wires that end beside it: CURRENT_SHIP, 4'b0000, main_1_p3
  // _4bit_greater_or_equal_than_and_less_than__main main_2: pin names not known; wires that end beside it: 4'b0100, CURRENT_SHIP
  // _4bit_greater_or_equal_than_and_less_than__main main_3: pin names not known; wires that end beside it: 4'b0100, 4'b0111, CURRENT_SHIP, main_3_p4
  // _4bit_greater_or_equal_than_and_less_than__main main_4: pin names not known; wires that end beside it: 4'b0111, 4'b1001, CURRENT_SHIP, 4'b1001, 4'b1010, main_4_p6, main_4_p7
  assign SAVE = not_5_out ? CONFIRM : 1'bz;  // Controlled_Buffer controlled_buffer_7
  not not_5 (not_5_out, CHECKING);
  assign SAVE = CHECKING ? OVERWRITE : 1'bz;  // Controlled_Buffer controlled_buffer_8
  Comparator #(.width(4)) comparator_1 (.a(CHECK_X), .b(VERT_CHECK[3:0]), .eq(comparator_1_eq));  // open: gt, lt
  Adder #(.width(4)) adder_1 (.a(VERT_CHECK[7:4]), .b(4'b0001), .out(adder_1_out));  // open: cin, cout
  Adder #(.width(4)) adder_2 (.a(VERT_CHECK[7:4]), .b(4'b0010), .out(adder_2_out));  // open: cin, cout
  Adder #(.width(4)) adder_3 (.a(VERT_CHECK[7:4]), .b(4'b0011), .out(adder_3_out));  // open: cin, cout
  Comparator #(.width(4)) comparator_2 (.a(CHECK_Y), .b(HORI_CHECK[7:4]), .eq(comparator_2_eq));  // open: gt, lt
  Adder #(.width(4)) adder_4 (.a(HORI_CHECK[3:0]), .b(4'b0001), .out(adder_4_out));  // open: cin, cout
  Adder #(.width(4)) adder_5 (.a(HORI_CHECK[3:0]), .b(4'b0010), .out(adder_5_out));  // open: cin, cout
  Adder #(.width(4)) adder_6 (.a(HORI_CHECK[3:0]), .b(4'b0011), .out(adder_6_out));  // open: cin, cout
  Pull_Resistor pull_resistor_1 (.node(SHIP_TYPE));
  assign SHIP_TYPE = main_1_p3 ? 2'b00 : 2'bz;  // Controlled_Buffer controlled_buffer_9
  Pull_Resistor pull_resistor_2 (.node(SHIP_TYPE));
  assign SHIP_TYPE = main_3_p4 ? 2'b01 : 2'bz;  // Controlled_Buffer controlled_buffer_10
  Pull_Resistor pull_resistor_3 (.node(SHIP_TYPE));
  assign SHIP_TYPE = main_4_p6 ? 2'b10 : 2'bz;  // Controlled_Buffer controlled_buffer_11
  Pull_Resistor pull_resistor_4 (.node(SHIP_TYPE));
  assign SHIP_TYPE = main_4_p7 ? 2'b11 : 2'bz;  // Controlled_Buffer controlled_buffer_12
  and and_8 (and_8_out, CLK, CHECKING);
  Comparator #(.width(4), .mode("unsigned")) comparator_3 (
    .a(CHECK_Y), .b(VERT_CHECK[7:4]), .eq(comparator_3_eq));  // open: gt, lt
  Comparator #(.width(4), .mode("unsigned")) comparator_4 (
    .a(CHECK_Y), .b(adder_1_out), .eq(comparator_4_eq));  // open: gt, lt
  Comparator #(.width(4), .mode("unsigned")) comparator_5 (
    .a(CHECK_Y), .b(adder_2_out), .eq(comparator_5_eq));  // open: gt, lt
  Comparator #(.width(4), .mode("unsigned")) comparator_6 (
    .a(CHECK_Y), .b(adder_3_out), .eq(comparator_6_eq));  // open: gt, lt
  Comparator #(.width(4), .mode("unsigned")) comparator_7 (
    .a(CHECK_X), .b(HORI_CHECK[3:0]), .eq(comparator_7_eq));  // open: gt, lt
  Comparator #(.width(4), .mode("unsigned")) comparator_8 (
    .a(CHECK_X), .b(adder_4_out), .eq(comparator_8_eq));  // open: gt, lt
  Comparator #(.width(4), .mode("unsigned")) comparator_9 (
    .a(CHECK_X), .b(adder_5_out), .eq(comparator_9_eq));  // open: gt, lt
  Comparator #(.width(4), .mode("unsigned")) comparator_10 (
    .a(CHECK_X), .b(adder_6_out), .eq(comparator_10_eq));  // open: gt, lt
  Counter #(.width(4), .max('ha), .trigger("falling")) counter_2 (
    .Q(CURR_SHIP_CHECK), .carry(CHECK_OCCUPIED_RST), .clk(CHECK_FRAME_END), .clr(CHECK_OCCUPIED_RST));  // open: load, D, count
  Counter #(.width(3), .max('h6), .trigger("falling")) counter_3 (
    .Q(counter_3_q), .carry(CHECK_FRAME_END), .clk(and_8_out));  // open: load, D, count, clr
  and and_9 (and_9_out, comparator_3_eq, ALIVE0);
  and and_10 (and_10_out, comparator_4_eq, ALIVE1);
  and and_11 (and_11_out, comparator_5_eq, ALIVE2);
  and and_12 (and_12_out, comparator_6_eq, ALIVE3);
  not not_6 (not_6_out, ROTATED_CHECK);
  and and_13 (and_13_out, comparator_7_eq, ALIVE0);
  and and_14 (and_14_out, comparator_8_eq, ALIVE1);
  and and_15 (and_15_out, comparator_9_eq, ALIVE2);
  and and_16 (and_16_out, comparator_10_eq, ALIVE3);
  Comparator #(.width(3), .mode("unsigned")) comparator_11 (
    .a(counter_3_q), .b(3'b001), .eq(comparator_11_eq));  // open: gt, lt
  Comparator #(.width(3), .mode("unsigned")) comparator_12 (
    .a(counter_3_q), .b(3'b010), .gt(MEM_NOT_CHANGING), .eq(comparator_12_eq));  // open: lt
  Multiplexer #(.enable("false")) multiplexer_2 (.in0(and_9_out), .in1(and_13_out), .out(_0HIT), .sel(not_6_out));
  Multiplexer #(.enable("false")) multiplexer_3 (.in0(and_10_out), .in1(and_14_out), .out(_1HIT), .sel(not_6_out));
  D_Flip_Flop d_ff_2 (
    .clk(comparator_11_eq), .D(comparator_11_eq), .Q(SAVE_CURR_RAM_STATE), .reset(comparator_12_eq));  // open: Qn, preset, en
  Multiplexer #(.enable("false")) multiplexer_4 (.in0(and_11_out), .in1(and_15_out), .out(_2HIT), .sel(not_6_out));
  Multiplexer #(.enable("false")) multiplexer_5 (.in0(and_12_out), .in1(and_16_out), .out(_3HIT), .sel(not_6_out));
  Counter #(.width(5), .max('h1f)) hits_counter (
    .Q(hits_counter_q), .clk(OVERWRITE));  // open: load, D, count, carry, clr
  D_Flip_Flop d_ff_3 (.clk(OVERWRITE), .D(OVERWRITE), .Q(HIT), .reset(CHECK));  // open: Qn, preset, en
  or or_3 (or_3_out, and_9_out, and_10_out, and_11_out, and_12_out);
  or or_4 (or_4_out, and_13_out, and_14_out, and_15_out, and_16_out);
  Comparator #(.width(5), .mode("unsigned")) comparator_13 (
    .a(hits_counter_q), .b(5'b10100), .eq(WIN));  // open: gt, lt
  and and_17 (and_17_out, MEM_NOT_CHANGING, ROTATED_CHECK, comparator_1_eq, or_3_out);
  and and_18 (and_18_out, MEM_NOT_CHANGING, ~ROTATED_CHECK, comparator_2_eq, or_4_out);  // AND_Gate
  D_Flip_Flop d_ff_4 (.clk(and_17_out), .D(and_17_out), .Q(VERT_HIT), .reset(CHECK_FRAME_END));  // open: Qn, preset, en
  D_Flip_Flop d_ff_5 (.clk(and_18_out), .D(and_18_out), .Q(HORI_HIT), .reset(CHECK_FRAME_END));  // open: Qn, preset, en

  // Other names for the same wires on the sheet: SHIP_X[3:0] = X; SHIP_Y[3:0] = Y; IS_ROTATED = ROTATED

  // Notes on the sheet:
  //   nieobrocony statek jest poziomy a obrocony pionowy
  //   specjalnie nie daje pull resistora bo wtedy pkaze X w (0,0)
  //   najpierw ram out powinien sie zmienic a potem powinno dopiero sie zapisac a jest odwrotnie i takie opoznienie jakby jest
  //   jak jest 20 overwritow(zatopionych) to znaczy ze win
endmodule
