// Logisim project not_hit_ram_storage.circ as structural Verilog: 1 circuit, main circuit main
module main (
  input  IF_1__save_input,
  input  CLR,
  input  [3:0] X,
  input  [3:0] Y,
  input  CLK,
  input  in_6,
  output [3:0] X_2,
  output [3:0] Y_2
);

  wire _0__REPEATS, CLK_t, comparator_2_lt, controlled_buffer_1_out, main_1_q, main_2_out_3, not_hit___0,
       or_1_out, or_2_out, pull_resistor_1_node, STORE_iF_EQUAL___HASN_T_APPEARED;
  wire [7:0] ADDRESS, DATA_TO_CHECK, ram_1_data, STABLE_COUNTER_q;

  Clock clock_1 (.out(CLK_t));
  Counter #(.width(1), .max('h1), .ongoal("stay")) count_form_0 (
    .carry(not_hit___0), .clk(IF_1__save_input), .clr(CLR));  // open: load, D, count, Q
  Pull_Resistor pull_resistor_1 (.node(pull_resistor_1_node));
  Comparator comparator_1 (.a(DATA_TO_CHECK), .b({Y_2, X_2}), .eq(pull_resistor_1_node));  // open: gt, lt
  or or_1 (or_1_out, in_6, CLR);
  Counter #(.max('h90)) STABLE_COUNTER (
    .Q(STABLE_COUNTER_q), .clk(controlled_buffer_1_out), .clr(CLR));  // open: load, D, count, carry
  assign controlled_buffer_1_out = not_hit___0 ? IF_1__save_input : 1'bz;  // Controlled_Buffer controlled_buffer_1
  Register register_1 (.D({Y, X}), .Q(DATA_TO_CHECK), .clk(IF_1__save_input), .clr(CLR));  // open: en
  SRlatch_main main_1 (.RESTET(or_1_out), .SET(pull_resistor_1_node), .Q(main_1_q));
  not not_1 (_0__REPEATS, main_1_q);
  Comparator comparator_2 (
    .a(STABLE_COUNTER_q), .b(ADDRESS), .eq(STORE_iF_EQUAL___HASN_T_APPEARED), .lt(comparator_2_lt));  // open: gt
  RAM #(.bus("separate")) ram_1 (
    .addr(ADDRESS), .din(DATA_TO_CHECK), .data(ram_1_data), .str(STORE_iF_EQUAL___HASN_T_APPEARED),
    .clk(CLK_t), .ld(1'b1), .clr(CLR));  // open: sel
  assign {Y_2, X_2} = not_hit___0 ? ram_1_data : 8'bz;  // Controlled_Buffer controlled_buffer_2
  tick_main main_2 (.in_1(CLK_t), .in_2(STORE_iF_EQUAL___HASN_T_APPEARED), .out_3(main_2_out_3));
  or or_2 (or_2_out, main_2_out_3, comparator_2_lt, IF_1__save_input, CLR);
  Counter #(.max('h90)) UNSTABLE_COUNTER (.Q(ADDRESS), .clk(CLK_t), .clr(or_2_out));  // open: load, D, count, carry

  // Other names for the same wires on the sheet: CHECKED = in_6; CURRENT_MEM_OUT[7:0] = {Y_2, X_2};
  //   nHIT = IF_1__save_input
endmodule
