// Logisim project przesuwanko.circ as structural Verilog: 1 circuit, main circuit main
module main (
  output [31:0] out_1
);

  wire and_1_out, and_2_out, CLK_out, DOWN, LEFT, or_1_out, or_2_out, RIGHT, undriven, UP;
  wire [4:0] multiplier_1_out, multiplier_2_out, XPOS, YPOS;
  wire [6:0] keyboard_1_data;
  wire [31:0] demultiplexer_1_out0, demultiplexer_1_out1, demultiplexer_1_out2, demultiplexer_1_out3,
       demultiplexer_1_out4, demultiplexer_1_out5, demultiplexer_1_out6, demultiplexer_1_out7,
       demultiplexer_1_out8, demultiplexer_1_out9, demultiplexer_1_out10, demultiplexer_1_out11,
       demultiplexer_1_out12, demultiplexer_1_out13, demultiplexer_1_out14, demultiplexer_1_out15,
       demultiplexer_1_out16, demultiplexer_1_out17, demultiplexer_1_out18, demultiplexer_1_out19,
       demultiplexer_1_out20, demultiplexer_1_out21, demultiplexer_1_out22, demultiplexer_1_out23,
       demultiplexer_1_out24, demultiplexer_1_out25, demultiplexer_1_out26, demultiplexer_1_out27,
       demultiplexer_1_out28, demultiplexer_1_out29, demultiplexer_1_out30, demultiplexer_1_out31;

  Multiplier #(.width(5)) multiplier_1 (.a(XPOS), .b(5'b00001), .out(multiplier_1_out));  // open: cin, cout
  DotMatrix #(.matrixcols(32), .matrixrows(32)) dotmatrix_1 (
    .col0(demultiplexer_1_out0), .col1(demultiplexer_1_out1), .col2(demultiplexer_1_out2),
    .col3(demultiplexer_1_out3), .col4(demultiplexer_1_out4), .col5(demultiplexer_1_out5),
    .col6(demultiplexer_1_out6), .col7(demultiplexer_1_out7), .col8(demultiplexer_1_out8),
    .col9(demultiplexer_1_out9), .col10(demultiplexer_1_out10), .col11(demultiplexer_1_out11),
    .col12(demultiplexer_1_out12), .col13(demultiplexer_1_out13), .col14(demultiplexer_1_out14),
    .col15(demultiplexer_1_out15), .col16(demultiplexer_1_out16), .col17(demultiplexer_1_out17),
    .col18(demultiplexer_1_out18), .col19(demultiplexer_1_out19), .col20(demultiplexer_1_out20),
    .col21(demultiplexer_1_out21), .col22(demultiplexer_1_out22), .col23(demultiplexer_1_out23),
    .col24(demultiplexer_1_out24), .col25(demultiplexer_1_out25), .col26(demultiplexer_1_out26),
    .col27(demultiplexer_1_out27), .col28(demultiplexer_1_out28), .col29(demultiplexer_1_out29),
    .col30(demultiplexer_1_out30), .col31(demultiplexer_1_out31));
  Multiplier #(.width(5)) multiplier_2 (.a(YPOS), .b(5'b00001), .out(multiplier_2_out));  // open: cin, cout
  Shifter #(.width(32), .shift("lr")) shifter_1 (.in(32'he0000000), .\dist (multiplier_2_out), .out(out_1));
  Demultiplexer #(.select(5), .width(32)) demultiplexer_1 (
    .out0(demultiplexer_1_out0), .out1(demultiplexer_1_out1), .out2(demultiplexer_1_out2),
    .out3(demultiplexer_1_out3), .out4(demultiplexer_1_out4), .out5(demultiplexer_1_out5),
    .out6(demultiplexer_1_out6), .out7(demultiplexer_1_out7), .out8(demultiplexer_1_out8),
    .out9(demultiplexer_1_out9), .out10(demultiplexer_1_out10), .out11(demultiplexer_1_out11),
    .out12(demultiplexer_1_out12), .out13(demultiplexer_1_out13), .out14(demultiplexer_1_out14),
    .out15(demultiplexer_1_out15), .out16(demultiplexer_1_out16), .out17(demultiplexer_1_out17),
    .out18(demultiplexer_1_out18), .out19(demultiplexer_1_out19), .out20(demultiplexer_1_out20),
    .out21(demultiplexer_1_out21), .out22(demultiplexer_1_out22), .out23(demultiplexer_1_out23),
    .out24(demultiplexer_1_out24), .out25(demultiplexer_1_out25), .out26(demultiplexer_1_out26),
    .out27(demultiplexer_1_out27), .out28(demultiplexer_1_out28), .out29(demultiplexer_1_out29),
    .out30(demultiplexer_1_out30), .out31(demultiplexer_1_out31), .in(out_1), .sel(multiplier_1_out));  // open: en
  and and_1 (and_1_out, 1'b1, LEFT);
  Counter #(.width(5), .max('h1f)) counter_1 (
    .load(and_1_out), .Q(XPOS), .clk(or_1_out));  // open: D, count, carry, clr
  or or_1 (or_1_out, LEFT, RIGHT);
  Clock CLK (.out(CLK_out));
  Keyboard #(.buflen(7)) keyboard_1 (.clk(CLK_out), .clr(undriven), .data(keyboard_1_data));  // open: re, avail
  KeyboardInputAWSD_main main_1 (
    .out_3(UP), .Down_pressed(DOWN), .Left_pressed(LEFT), .Right_pressed(RIGHT),
    .Keyboard_out(keyboard_1_data), .Keyboard_rst(undriven));
  and and_2 (and_2_out, 1'b1, UP);
  or or_2 (or_2_out, UP, DOWN);
  Counter #(.width(5), .max('h1f)) counter_2 (
    .load(and_2_out), .Q(YPOS), .clk(or_2_out));  // open: D, count, carry, clr

  // Notes on the sheet:
  //   X POSITION
  //   FIELD SIZE X
  //   FIELD SIZE Y
  //   Y POSITION
endmodule
